// Logisim project LC-2200-32.circ as structural Verilog: 8 circuits, main circuit Processor
module Processor (
  input  Clock,
  input  [1:0] RegSel,
  input  LdA,
  input  LdB,
  input  DrPC,
  input  [1:0] ALUFunc,
  input  LdMAR,
  input  DrREG,
  input  WrREG,
  input  LdPC,
  input  DrMEM,
  input  WrMEM,
  input  LdIR,
  input  DrALU,
  input  IntAck,
  input  LdZ,
  input  DrOFF,
  input  LdEnInt,
  input  DrEnInt,
  input  [31:0] DeviceIndex,
  output Z,
  output [3:0] Rx,
  output [3:0] Ry,
  output [3:0] Rz,
  output [3:0] Opcode,
  output IE
);

  wire Clr, comparator_1_lt, comparator_2_eq, not_1_out;
  wire [3:0] RegNo;
  wire [19:4] IR_q;
  wire [31:0] Bus, multiplexer_1_out, OutA, OutALU, OutB, OutMAR, OutMEM, OutOFF, OutPC, OutREG;

  Register #(.width(32)) PC (.D(Bus), .en(LdPC), .Q(OutPC), .clk(Clock), .clr(Clr));
  Button button_1 (.out(Clr));
  Comparator #(.width(32), .mode("unsigned")) comparator_1 (
    .a(OutPC), .b(32'h10), .lt(comparator_1_lt));  // open: gt, eq
  Multiplexer #(.width(32), .enable("false")) multiplexer_1 (
    .in0(OutPC), .in1(32'h10), .out(multiplexer_1_out), .sel(comparator_1_lt));
  assign Bus = DrPC ? multiplexer_1_out : 32'bz;  // Controlled_Buffer PCBuff
  Register #(.width(32)) A (.D(Bus), .en(LdA), .Q(OutA), .clk(Clock), .clr(Clr));
  ALU alu_1 (.FUNC(ALUFunc), .INPUT_A(OutA), .INPUT_B(OutB), .out_4(OutALU));
  assign Bus = DrALU ? OutALU : 32'bz;  // Controlled_Buffer ALUBuff
  Register #(.width(32)) B (.D(Bus), .en(LdB), .Q(OutB), .clk(Clock), .clr(Clr));
  Comparator #(.width(32), .mode("unsigned")) comparator_2 (
    .a(OutALU), .b({32{1'b0}}), .eq(comparator_2_eq));  // open: gt, lt
  Registers registers_1 (
    .WrReg(WrREG), .RegSel1(RegNo), .Data_Out_1(OutREG), .Data_In(Bus), .Clock(Clock), .ClearRegFile(Clr));
  assign Bus = DrREG ? OutREG : 32'bz;  // Controlled_Buffer REGBuff
  Register #(.width(1)) Z_Register (.D(comparator_2_eq), .en(LdZ), .Q(Z), .clk(Clock), .clr(Clr));
  Multiplexer #(.select(2), .width(4), .enable("false")) multiplexer_2 (
    .in0(Rx), .in1(Ry), .in2(Rz), .out(RegNo), .sel(RegSel));  // open: in3
  Register #(.width(32)) MAR (.D(Bus), .en(LdMAR), .Q(OutMAR), .clk(Clock), .clr(Clr));
  RAM #(.addrWidth(24), .dataWidth(32), .bus("separate")) ram_1 (
    .addr(OutMAR[23:0]), .din(Bus), .data(OutMEM), .str(WrMEM), .clk(Clock), .ld(not_1_out), .clr(Clr));  // open: sel
  not not_1 (not_1_out, WrMEM);
  assign Bus = DrMEM ? OutMEM : 32'bz;  // Controlled_Buffer MEMBuff
  Register #(.width(1)) u_IE (.D(DrEnInt), .en(LdEnInt), .Q(IE), .clk(Clock));  // open: clr
  Register #(.width(32)) IR (.D(Bus), .en(LdIR), .Q({Opcode, Rx, Ry, IR_q, Rz}), .clk(Clock), .clr(Clr));
  Multiplexer #(.select(2), .width(4), .enable("false")) multiplexer_3 (
    .in0(Rx), .in1(Ry), .in2(Rz), .in3(4'b1100), .out(RegNo), .sel(RegSel));
  assign Bus = DrOFF ? OutOFF : 32'bz;  // Controlled_Buffer OFFBuff
  assign OutOFF = {{12{1'b0}}, {IR_q, Rz}};  // Bit_Extender bit_extender_1
  assign Bus = IntAck ? DeviceIndex : 32'bz;  // Controlled_Buffer EnIntBuff

  // Other names for the same wires on the sheet: ZeroDetect[31:0] = OutALU

  // Notes on the sheet:
  //   Thanh Ky Quan
  //   902977469
  //   00: ADD
  //   01:NAND
  //   10: SUB
  //   11: INC
  //   00 = RX
  //   01 = RY
  //   10 = RZ
  //   11=$k0
endmodule

module ALU (
  input  [31:0] INPUT_A,
  input  [31:0] INPUT_B,
  input  [1:0] FUNC,
  output [31:0] out_4
);

  wire [31:0] adder_1_out, adder_2_out, nand_1_out, subtractor_1_out;

  Adder #(.width(32)) adder_1 (.a(INPUT_A), .b(INPUT_B), .out(adder_1_out));  // open: cin, cout
  assign nand_1_out = ~(INPUT_A & INPUT_B);  // NAND_Gate nand_1, 32 bits wide
  Multiplexer #(.select(2), .width(32), .enable("false")) multiplexer_1 (
    .in0(adder_1_out), .in1(nand_1_out), .in2(subtractor_1_out), .in3(adder_2_out), .out(out_4), .sel(FUNC));
  Subtractor #(.width(32)) subtractor_1 (.a(INPUT_A), .b(INPUT_B), .out(subtractor_1_out));  // open: bin, bout
  Adder #(.width(32)) adder_2 (.a(INPUT_A), .b(32'h1), .out(adder_2_out));  // open: cin, cout
endmodule

module State_Machine (
  input  Clock,
  input  [3:0] OpCode,
  input  Z,
  input  Int,
  output DrREG,
  output DrMEM,
  output DrALU,
  output DrPC,
  output DrOFF,
  output LdPC,
  output LdIR,
  output LdMAR,
  output LdA,
  output LdB,
  output LdZ,
  output WrREG,
  output WrMEM,
  output [1:0] RegSel,
  output [1:0] ALU_FUNC,
  output LdEnInt,
  output DrEnInt,
  output IntAck
);

  wire checkZ, OpTest;
  wire [5:0] multiplexer_1_out, register_1_q, rom_1_data, rom_2_data, rom_3_data, rom_4_data;

  Register #(.width(6)) register_1 (.D(multiplexer_1_out), .en(Clock), .Q(register_1_q), .clk(Clock));  // open: clr
  Multiplexer #(.select(2), .width(6), .enable("false")) multiplexer_1 (
    .in0(rom_1_data), .in1(rom_2_data), .in2(rom_3_data), .in3(rom_4_data), .out(multiplexer_1_out),
    .sel({checkZ, OpTest}));
  ROM #(.addrWidth(6), .dataWidth(28)) rom_1 (
    .addr(register_1_q),
    .data({IntAck, DrEnInt, LdEnInt, checkZ, OpTest, ALU_FUNC, RegSel, WrMEM, WrREG, LdZ, LdB, LdA, LdMAR, LdIR, LdPC, DrOFF, DrPC, DrALU, DrMEM, DrREG, rom_1_data}));  // open: sel
  ROM #(.addrWidth(4), .dataWidth(6)) rom_2 (.addr(OpCode), .data(rom_2_data));  // open: sel
  ROM #(.addrWidth(2), .dataWidth(6)) rom_3 (.addr({1'b0, Z}), .data(rom_3_data));  // open: sel
  ROM #(.addrWidth(2), .dataWidth(6)) rom_4 (.addr({1'b0, Int}), .data(rom_4_data));  // open: sel

  // Notes on the sheet:
  //   Thanh Ky Quan
  //   902977469
  //   contents of rom_1 (hex, n*v repeats v):
  //   1800000 6202 1083 e00900 21a0205 8002006 800880 84048 108049 20100 8404b 10804c 420100 8c04e 20410f
  //   620100 0 84052 8413 420100 84055 108056 220100 84058 8419 20100 8405b 841c 211d 20080 8405f 8420
  //   2121 40040 4063 88064 410125 1000000 4227 8428 900 a022a 840 2b 6000000 2000000 6180840
  //   contents of rom_2 (hex, n*v repeats v):
  //   7 14 17 1a 1e 22 29 2b a 10 2c 2d 2e 11 d
  //   contents of rom_3 (hex, n*v repeats v):
  //   0 26
  //   contents of rom_4 (hex, n*v repeats v):
  //   1 4
endmodule

// 0?
module Zero_Detection (
  input  [31:0] In,
  output Out
);

  Comparator #(.width(32), .mode("unsigned")) comparator_1 (.a(In), .b({32{1'b0}}), .eq(Out));  // open: gt, lt
endmodule

// Reg File
module Registers (
  input  [31:0] Data_In,
  input  WrReg,
  input  [3:0] RegSel1,
  input  Clock,
  input  ClearRegFile,
  output [31:0] Data_Out_1
);

  wire and_1_out, and_2_out, and_3_out, and_4_out, and_5_out, and_6_out, and_7_out, and_8_out, and_9_out,
       and_10_out, and_11_out, and_12_out, and_13_out, and_14_out, and_15_out, and_16_out, S1_0, S1_1, S1_2,
       S1_3, S1_4, S1_5, S1_6, S1_7, S1_8, S1_9, S1_10, S1_11, S1_12, S1_13, S1_14, S1_15;
  wire [31:0] a0, a1, a2, at, k0, pr, ra, s0, s1, s2, sp, t0, t1, t2, v0, zero;

  Decoder #(.select(4), .enable("false")) decoder_1 (
    .out0(S1_0), .out1(S1_1), .out2(S1_2), .out3(S1_3), .out4(S1_4), .out5(S1_5), .out6(S1_6), .out7(S1_7),
    .out8(S1_8), .out9(S1_9), .out10(S1_10), .out11(S1_11), .out12(S1_12), .out13(S1_13), .out14(S1_14),
    .out15(S1_15), .sel(RegSel1));
  Multiplexer #(.select(4), .width(32), .enable("false")) multiplexer_1 (
    .in0(zero), .in1(at), .in2(v0), .in3(a0), .in4(a1), .in5(a2), .in6(t0), .in7(t1), .in8(t2), .in9(s0),
    .in10(s1), .in11(s2), .in12(k0), .in13(sp), .in14(pr), .in15(ra), .out(Data_Out_1), .sel(RegSel1));
  and and_1 (and_1_out, S1_0, WrReg);
  and and_2 (and_2_out, S1_1, WrReg);
  and and_3 (and_3_out, S1_2, WrReg);
  and and_4 (and_4_out, S1_3, WrReg);
  and and_5 (and_5_out, S1_4, WrReg);
  and and_6 (and_6_out, S1_5, WrReg);
  and and_7 (and_7_out, S1_6, WrReg);
  and and_8 (and_8_out, S1_7, WrReg);
  and and_9 (and_9_out, S1_8, WrReg);
  and and_10 (and_10_out, S1_9, WrReg);
  and and_11 (and_11_out, S1_10, WrReg);
  and and_12 (and_12_out, S1_11, WrReg);
  and and_13 (and_13_out, S1_12, WrReg);
  and and_14 (and_14_out, S1_13, WrReg);
  and and_15 (and_15_out, S1_14, WrReg);
  and and_16 (and_16_out, S1_15, WrReg);
  Register #(.width(32)) u_zero (.D(Data_In), .en(and_1_out), .Q(zero), .clk(Clock), .clr(1'b1));
  Register #(.width(32)) u_at (.D(Data_In), .en(and_2_out), .Q(at), .clk(Clock), .clr(ClearRegFile));
  Register #(.width(32)) u_v0 (.D(Data_In), .en(and_3_out), .Q(v0), .clk(Clock), .clr(ClearRegFile));
  Register #(.width(32)) u_a0 (.D(Data_In), .en(and_4_out), .Q(a0), .clk(Clock), .clr(ClearRegFile));
  Register #(.width(32)) u_a1 (.D(Data_In), .en(and_5_out), .Q(a1), .clk(Clock), .clr(ClearRegFile));
  Register #(.width(32)) u_a2 (.D(Data_In), .en(and_6_out), .Q(a2), .clk(Clock), .clr(ClearRegFile));
  Register #(.width(32)) u_t0 (.D(Data_In), .en(and_7_out), .Q(t0), .clk(Clock), .clr(ClearRegFile));
  Register #(.width(32)) u_t1 (.D(Data_In), .en(and_8_out), .Q(t1), .clk(Clock), .clr(ClearRegFile));
  Register #(.width(32)) u_t2 (.D(Data_In), .en(and_9_out), .Q(t2), .clk(Clock), .clr(ClearRegFile));
  Register #(.width(32)) u_s0 (.D(Data_In), .en(and_10_out), .Q(s0), .clk(Clock), .clr(ClearRegFile));
  Register #(.width(32)) u_s1 (.D(Data_In), .en(and_11_out), .Q(s1), .clk(Clock), .clr(ClearRegFile));
  Register #(.width(32)) u_s2 (.D(Data_In), .en(and_12_out), .Q(s2), .clk(Clock), .clr(ClearRegFile));
  Register #(.width(32)) u_k0 (.D(Data_In), .en(and_13_out), .Q(k0), .clk(Clock), .clr(ClearRegFile));
  Register #(.width(32)) u_sp (.D(Data_In), .en(and_14_out), .Q(sp), .clk(Clock), .clr(ClearRegFile));
  Register #(.width(32)) u_pr (.D(Data_In), .en(and_15_out), .Q(pr), .clk(Clock), .clr(ClearRegFile));
  Register #(.width(32)) u_ra (.D(Data_In), .en(and_16_out), .Q(ra), .clk(Clock), .clr(ClearRegFile));

  // Other names for the same wires on the sheet: Din[31:0] = Data_In; en = WrReg
endmodule

module Intergenerator (
  input  CLK,
  output IntOut
);

  wire [9:0] adder_1_out, register_1_q;

  Adder #(.width(10)) adder_1 (.a(10'h1), .b(register_1_q), .out(adder_1_out));  // open: cin, cout
  Register #(.width(10)) register_1 (.D(adder_1_out), .en(1'b1), .Q(register_1_q), .clk(CLK));  // open: clr
  Comparator #(.width(10), .mode("unsigned")) comparator_1 (.a(10'h3), .b(register_1_q), .eq(IntOut));  // open: gt, lt
endmodule

module main (
);

  wire and_1_out, Clock, DrALU, DrEnInt, DrMEM, DrOFF, DrPC, DrREG, IntAck, IntEn, Interrupt,
       state_machine_1_lda, state_machine_1_ldb, state_machine_1_ldenint, state_machine_1_ldir,
       state_machine_1_ldmar, state_machine_1_ldpc, state_machine_1_ldz, WrMEM, WrREG, Z;
  wire [1:0] ALUFunc, RegSel;
  wire [3:0] OPCode, Rx, Ry, Rz;
  wire [31:0] DeviceIndex;

  State_Machine state_machine_1 (
    .Clock(Clock), .OpCode(OPCode), .Z(Z), .Int(and_1_out), .DrREG(DrREG), .DrMEM(DrMEM), .DrALU(DrALU),
    .DrPC(DrPC), .DrOFF(DrOFF), .LdPC(state_machine_1_ldpc), .LdIR(state_machine_1_ldir),
    .LdMAR(state_machine_1_ldmar), .LdA(state_machine_1_lda), .LdB(state_machine_1_ldb),
    .LdZ(state_machine_1_ldz), .WrREG(WrREG), .WrMEM(WrMEM), .RegSel(RegSel), .ALU_FUNC(ALUFunc),
    .LdEnInt(state_machine_1_ldenint), .DrEnInt(DrEnInt), .IntAck(IntAck));
  Clock u_CLOCK (.out(Clock));
  and and_1 (and_1_out, Interrupt, IntEn);
  Processor processor_1 (
    .Clock(Clock), .RegSel(RegSel), .LdA(state_machine_1_lda), .Z(Z), .LdB(state_machine_1_ldb), .DrPC(DrPC),
    .ALUFunc(ALUFunc), .LdMAR(state_machine_1_ldmar), .Rx(Rx), .DrREG(DrREG), .WrREG(WrREG),
    .LdPC(state_machine_1_ldpc), .Ry(Ry), .DrMEM(DrMEM), .WrMEM(WrMEM), .LdIR(state_machine_1_ldir), .Rz(Rz),
    .DrALU(DrALU), .LdZ(state_machine_1_ldz), .Opcode(OPCode), .DrOFF(DrOFF), .IntAck(IntAck),
    .DrEnInt(DrEnInt), .LdEnInt(state_machine_1_ldenint), .DeviceIndex(DeviceIndex), .IE(IntEn));
  device device_1 (.Interrupt(Interrupt), .DeviceIndex(DeviceIndex), .IntAck(IntAck), .Clock(Clock));
endmodule

module device (
  input  Clock,
  input  IntAck,
  output Interrupt,
  output [31:0] DeviceIndex
);

  wire intergenerator_1_intout;

  assign DeviceIndex = IntAck ? 32'h1 : 32'bz;  // Controlled_Buffer controlled_buffer_1
  Intergenerator intergenerator_1 (.IntOut(intergenerator_1_intout), .CLK(Clock));
  Register #(.width(1)) INT (.D(intergenerator_1_intout), .en(IntAck), .Q(Interrupt), .clk(Clock));  // open: clr
endmodule
