// Logisim project LC-2200-16.circ as structural Verilog: 4 circuits, main circuit main
module main (
);

  wire ALUHi, ALULo, checkZ, Clock, DrALU, DrMEM, DrOFF, DrPC, DrREG, LdA, LdB, LdIR, LdMAR, LdPC, LdZ,
       OpTest, RegSelHi, RegSelLo, WrMEM, WrREG, Z;
  wire [2:0] Opcode;
  wire [3:0] datapath_1_rx, datapath_1_ry, datapath_1_rz, RegNo;

  DataPath datapath_1 (
    .RegNo(RegNo), .LdA(LdB), .LdB(LdA), .DrPC(DrPC), .ALUFunc({ALUHi, ALULo}), .LdMAR(LdMAR), .DrREG(DrREG),
    .WrREG(WrREG), .LdPC(LdPC), .DrMEM(DrMEM), .WrMEM(WrMEM), .LdIR(LdIR), .DrALU(DrALU), .DrOFF(DrOFF),
    .LdZ(LdZ), .OutZ(Z), .Rx(datapath_1_rx), .Ry(datapath_1_ry), .Rz(datapath_1_rz), .Opcode(Opcode),
    .Clock(Clock));
  Multiplexer #(.select(2), .width(4), .enable("false")) multiplexer_1 (
    .in0(datapath_1_rx), .in1(datapath_1_ry), .in2(datapath_1_rz), .out(RegNo), .sel({RegSelHi, RegSelLo}));  // open: in3
  MicrocontrolUnit microcontrolunit_1 (
    .Z(Z), .OpCodeADDR(Opcode), .DrREG(DrREG), .LdA(LdA), .DrMEM(DrMEM), .LdB(LdB), .DrALU(DrALU), .LdZ(LdZ),
    .DrPC(DrPC), .WrREG(WrREG), .DrOFF(DrOFF), .WrMEM(WrMEM), .LdPC(LdPC), .ALULo(ALULo), .LdIR(LdIR),
    .ALUHi(ALUHi), .LdMAR(LdMAR), .OPTest(OpTest), .RegSelLo(RegSelLo), .chkZ(checkZ), .RegSelHi(RegSelHi),
    .Clock(Clock));
  Clock clock_1 (.out(Clock));
endmodule

module ALU (
  input  [15:0] A,
  input  [15:0] B,
  input  [1:0] Function,
  output [15:0] Output
);

  wire [15:0] ADD, INCREMENT, NAND, not_1_out, SUBTRACT;

  assign not_1_out = ~B;  // NOT_Gate not_1, 16 bits wide
  Multiplexer #(.select(2), .width(16), .enable("false")) multiplexer_1 (
    .in0(ADD), .in1(NAND), .in2(SUBTRACT), .in3(INCREMENT), .out(Output), .sel(Function));
  Adder #(.width(16)) adder_1 (.a(A), .b(B), .out(ADD), .cin(1'b0));  // open: cout
  assign NAND = ~(A & B);  // NAND_Gate nand_1, 16 bits wide
  Adder #(.width(16)) adder_2 (.a(A), .b(not_1_out), .out(SUBTRACT), .cin(1'b1));  // open: cout
  Adder #(.width(16)) adder_3 (.a(A), .b({16{1'b0}}), .out(INCREMENT), .cin(1'b1));  // open: cout

  // Notes on the sheet:
  //   16 bits ALU
endmodule

module DataPath (
  input  Clock,
  input  [3:0] RegNo,
  input  LdA,
  input  LdB,
  input  DrPC,
  input  [1:0] ALUFunc,
  input  LdMAR,
  input  DrREG,
  input  WrREG,
  input  LdPC,
  input  DrMEM,
  input  WrMEM,
  input  LdIR,
  input  DrALU,
  input  LdZ,
  input  DrOFF,
  output OutZ,
  output [3:0] Rx,
  output [3:0] Ry,
  output [3:0] Rz,
  output [2:0] Opcode
);

  wire button_1_out, comparator_1_eq, comparator_2_eq, not_1_out, not_2_out;
  wire [4:4] IR_q;
  wire [15:0] A_q, alu_1_output, B_q, bit_extender_1_out, controlled_buffer_1_out, multiplexer_1_out, OutMAR,
       PC_q, ram_1_data, ram_2_data;

  Register #(.width(16)) PC (.D(controlled_buffer_1_out), .en(LdPC), .Q(PC_q), .clk(Clock));  // open: clr
  assign controlled_buffer_1_out = DrPC ? PC_q : 16'bz;  // Controlled_Buffer controlled_buffer_1
  Register #(.width(16)) A (.D(controlled_buffer_1_out), .en(LdA), .Q(A_q), .clk(Clock));  // open: clr
  Comparator #(.width(16)) comparator_1 (
    .a(controlled_buffer_1_out), .b({16{1'b0}}), .eq(comparator_1_eq));  // open: gt, lt
  Register #(.width(16)) B (.D(controlled_buffer_1_out), .en(LdB), .Q(B_q), .clk(Clock));  // open: clr
  ALU alu_1 (.Function(ALUFunc), .Output(alu_1_output), .A(A_q), .B(B_q));
  assign controlled_buffer_1_out = DrALU ? alu_1_output : 16'bz;  // Controlled_Buffer controlled_buffer_2
  Register #(.width(1)) Z (.D(comparator_1_eq), .en(LdZ), .Q(OutZ), .clk(Clock));  // open: clr
  Comparator #(.width(4)) comparator_2 (.a(RegNo), .b(4'b0000), .eq(comparator_2_eq));  // open: gt, lt
  assign controlled_buffer_1_out = DrREG ? multiplexer_1_out : 16'bz;  // Controlled_Buffer controlled_buffer_3
  RAM #(.addrWidth(4), .dataWidth(16), .bus("separate")) ram_1 (
    .addr(RegNo), .din(controlled_buffer_1_out), .data(ram_1_data), .str(WrREG), .clk(Clock),
    .clr(button_1_out));  // open: sel, ld
  Button button_1 (.out(button_1_out));
  not not_1 (not_1_out, comparator_2_eq);
  Multiplexer #(.width(16), .enable("false")) multiplexer_1 (
    .in1(ram_1_data), .out(multiplexer_1_out), .sel(not_1_out));  // open: in0
  not not_2 (not_2_out, WrMEM);
  Register #(.width(16)) MAR (.D(controlled_buffer_1_out), .en(LdMAR), .Q(OutMAR), .clk(Clock));  // open: clr
  RAM #(.addrWidth(16), .dataWidth(16)) ram_2 (
    .addr(OutMAR), .data(ram_2_data), .clk(Clock), .ld(not_2_out));  // open: sel, clr
  assign controlled_buffer_1_out = DrMEM ? ram_2_data : 16'bz;  // Controlled_Buffer controlled_buffer_4
  Register #(.width(16)) IR (
    .D(controlled_buffer_1_out), .en(LdIR), .Q({Opcode, Rx, Ry, IR_q[4], Rz}), .clk(Clock));  // open: clr
  assign bit_extender_1_out = {{11{IR_q[4]}}, {IR_q[4], Rz}};  // Bit_Extender bit_extender_1
  assign controlled_buffer_1_out = DrOFF ? bit_extender_1_out : 16'bz;  // Controlled_Buffer controlled_buffer_5

  // Other names for the same wires on the sheet: Clk = Clock

  // Notes on the sheet:
  //   Bus
endmodule

module MicrocontrolUnit (
  input  Z,
  input  [2:0] OpCodeADDR,
  input  Clock,
  output DrREG,
  output LdPC,
  output DrMEM,
  output LdIR,
  output DrALU,
  output LdMAR,
  output RegSelLo,
  output DrPC,
  output LdA,
  output RegSelHi,
  output DrOFF,
  output LdB,
  output ALULo,
  output LdZ,
  output ALUHi,
  output OPTest,
  output WrREG,
  output chkZ,
  output WrMEM
);

  wire [5:0] multiplexer_1_out, NextState, OutOpCode, State, ZCode;

  ROM #(.addrWidth(6), .dataWidth(25)) rom_1 (
    .addr(State),
    .data({chkZ, OPTest, ALUHi, ALULo, RegSelHi, RegSelLo, WrMEM, WrREG, LdZ, LdB, LdA, LdMAR, LdIR, LdPC, DrOFF, DrPC, DrALU, DrMEM, DrREG, NextState}));  // open: sel
  ROM #(.addrWidth(3), .dataWidth(6)) rom_2 (.addr(OpCodeADDR), .data(OutOpCode));  // open: sel
  ROM #(.addrWidth(2), .dataWidth(6)) rom_3 (.addr({1'b0, Z}), .data(ZCode));  // open: sel
  Multiplexer #(.select(2), .width(6)) multiplexer_1 (
    .in0(NextState), .in1(OutOpCode), .in2(ZCode), .out(multiplexer_1_out), .sel({chkZ, OPTest}));  // open: in3, en
  Register #(.width(6)) State_Register (.D(multiplexer_1_out), .Q(State), .clk(Clock));  // open: en, clr

  // Notes on the sheet:
  //   Main ROM
  //   Opcode
  //   Check Z
  //   contents of rom_1 (hex, n*v repeats v):
  //   6201 1082 e00900 84044 108045 20100 84047 8408 20100 8404a 10804b 220100 a020d 840 8404f 8410 2111
  //   20080 84053 8414 2115 40040 4057 88058 1410100 6201 421b 841c 900 1d
  //   contents of rom_2 (hex, n*v repeats v):
  //   3 9 6 e 12 16 c 1d
  //   contents of rom_3 (hex, n*v repeats v):
  //   19 1a
endmodule
